// Logisim project circuit.circ as structural Verilog: 1 circuit, main circuit main
module main (
  input  [31:0] Number,
  input  [31:0] Multiplicand,
  output [31:0] result1,
  output [31:0] result_bigger_part
);

  wire clock_1_out;

  Clock clock_1 (.out(clock_1_out));
endmodule
