// Logisim project full_adder.circ as structural Verilog: 1 circuit, main circuit full_adder_2
module full_adder_2 (
  output [31:0] out_1,
  output [31:0] out_2
);

  wire [31:0] nand_1_out, nand_2_out, nand_3_out;

  assign nand_1_out = ~(32'h32 & 32'h1);  // NAND_Gate nand_1, 32 bits wide
  assign nand_2_out = ~(32'h32 & nand_1_out);  // NAND_Gate nand_2, 32 bits wide
  assign nand_3_out = ~(nand_1_out & 32'h1);  // NAND_Gate nand_3, 32 bits wide
  assign out_1 = ~(nand_2_out & nand_3_out);  // NAND_Gate nand_4, 32 bits wide
  assign out_2 = ~(nand_1_out & nand_1_out);  // NAND_Gate nand_5, 32 bits wide
endmodule
