// Logisim project final_project.circ as structural Verilog: 11 circuits, main circuit main
module main (
  input  [7:0] _1,
  input  [7:0] _2,
  input  [7:0] _3,
  input  [7:0] _4,
  input  [7:0] _5,
  input  [7:0] _6,
  input  [7:0] _7,
  input  [7:0] _8,
  input  clock,
  input  letter_first,
  input  letter_second,
  input  led_check,
  input  line_check,
  input  letter_third,
  input  [4:0] letter_choose,
  output a,
  output b,
  output c,
  output d,
  output e,
  output [6:0] tty,
  output f,
  output g,
  output led_1,
  output H,
  output led_2,
  output led_3,
  output letter_equal,
  output letter_equal_2,
  output led_4,
  output led_5,
  output [7:0] fail_times
);

  wire comparator_10_eq, comparator_10_gt, comparator_11_eq, comparator_11_gt, comparator_12_eq,
       comparator_12_gt, comparator_13_eq, comparator_13_gt;
  wire [7:0] multiplexer_1_out, multiplexer_2_out, multiplexer_3_out;

  Multiplexer #(.select(5), .width(8)) multiplexer_1 (
    .in0(8'h41), .in1(8'h42), .in2(8'h43), .in3(8'h44), .in4(8'h45), .in5(8'h46), .in6(8'h47), .in7(8'h48),
    .in8(8'h49), .in9(8'h4a), .in10(8'h4b), .in11(8'h4c), .in12(8'h4d), .in13(8'h4e), .in14(8'h4f),
    .in15(8'h50), .in16(8'h51), .in17(8'h52), .in18(8'h53), .in19(8'h54), .in20(8'h55), .in21(8'h56),
    .in22(8'h57), .in23(8'h58), .in24(8'h59), .in25(8'h5a), .out(multiplexer_1_out), .sel(letter_choose),
    .en(1'b1));  // open: in26, in27, in28, in29, in30, in31
  Multiplexer #(.select(3), .width(8)) multiplexer_2 (
    .in0(_1), .in1(_2), .in2(_3), .in3(_4), .in4(_5), .in5(_6), .in6(_7), .in7(_8), .out(multiplexer_2_out),
    .sel({letter_third, letter_second, letter_first}), .en(1'b1));
  Comparator comparator_1 (.a(_1), .b({8{1'b0}}), .eq(a));  // open: gt, lt
  Comparator comparator_2 (.a(_2), .b({8{1'b0}}), .eq(b));  // open: gt, lt
  Comparator comparator_3 (.a(_3), .b({8{1'b0}}), .eq(c));  // open: gt, lt
  Comparator comparator_4 (.a(_4), .b({8{1'b0}}), .eq(d));  // open: gt, lt
  Comparator comparator_5 (.a(_5), .b({8{1'b0}}), .eq(e));  // open: gt, lt
  Comparator comparator_6 (.a(_6), .b({8{1'b0}}), .eq(f));  // open: gt, lt
  Comparator comparator_7 (.a(_7), .b({8{1'b0}}), .eq(g));  // open: gt, lt
  Comparator comparator_8 (.a(_8), .b({8{1'b0}}), .eq(H));  // open: gt, lt
  Comparator comparator_9 (.a(multiplexer_2_out), .b(multiplexer_1_out), .eq(letter_equal));  // open: gt, lt
  Bit_Extender #(.out_width(7)) bit_extender_1 (.in(multiplexer_3_out), .out(tty));
  Multiplexer #(.select(2), .width(8)) multiplexer_3 (
    .in0(multiplexer_2_out), .in1(8'h5f), .in2(8'hd), .out(multiplexer_3_out), .sel({line_check, led_check}),
    .en(1'b1));  // open: in3
  Counter counter_1 (.D(fail_times), .count(led_check), .Q(fail_times), .clk(clock));  // open: load, carry, clr
  Comparator comparator_10 (.a(fail_times), .b(8'h1), .gt(comparator_10_gt), .eq(comparator_10_eq));  // open: lt
  Comparator comparator_11 (.a(fail_times), .b(8'h2), .gt(comparator_11_gt), .eq(comparator_11_eq));  // open: lt
  Comparator comparator_12 (.a(fail_times), .b(8'h3), .gt(comparator_12_gt), .eq(comparator_12_eq));  // open: lt
  Comparator comparator_13 (.a(fail_times), .b(8'h4), .gt(comparator_13_gt), .eq(comparator_13_eq));  // open: lt
  Comparator comparator_14 (.a(fail_times), .b(8'h5), .eq(led_5));  // open: gt, lt
  or or_1 (led_1, comparator_10_gt, comparator_10_eq);
  or or_2 (led_2, comparator_11_gt, comparator_11_eq);
  or or_3 (led_3, comparator_12_gt, comparator_12_eq);
  or or_4 (led_4, comparator_13_gt, comparator_13_eq);

  assign letter_equal_2 = letter_equal;
endmodule

module buradan_baslatin (
  input  [7:0] kelime_burdan_verilicek,
  input  [7:0] in_2,
  input  [7:0] in_3,
  input  [7:0] in_4,
  input  [7:0] in_5,
  input  [7:0] in_6,
  input  [7:0] in_7,
  input  [7:0] in_8,
  input  _0_olmali,
  output [7:0] error_times
);

  wire B_out, C_out, clock_fsm_1_clock, clock_fsm_1_tty_display_enable, comparator_1_eq, control_unit_2_1_n0,
       control_unit_2_1_n1, control_unit_2_1_n2, control_unit_2_1_n3, control_unit_2_1_n4,
       control_unit_3_1_n0, control_unit_3_1_n1, control_unit_3_1_n2, control_unit_3_1_n3,
       control_unit_3_1_n4, control_unit_4_1_n0, control_unit_4_1_n1, control_unit_4_1_n2,
       control_unit_4_1_n3, control_unit_4_1_n4, control_unit_5_1_n0, control_unit_5_1_n1,
       control_unit_5_1_n2, control_unit_5_1_n3, control_unit_5_1_n4, control_unit_6_1_n0,
       control_unit_6_1_n1, control_unit_6_1_n2, control_unit_6_1_n3, control_unit_6_1_n4, D_out, E_out,
       F_out, G_out, H_out, I_out, J_out, K_out, L_out, letter_control_unit_1_letter_first,
       letter_control_unit_1_letter_second, letter_control_unit_1_letter_third, M_out, main_1_a, main_1_b,
       main_1_c, main_1_d, main_1_e, main_1_f, main_1_g, main_1_h, main_1_led_1, main_1_led_2, main_1_led_3,
       main_1_led_4, main_1_led_5, main_1_letter_equal, main_1_letter_equal_2, N_out, not_1_out, not_2_out,
       not_3_out, not_4_out, not_5_out, not_6_out, not_7_out, not_8_out, not_9_out, O_out, P_out, Q_out,
       R_out, S_out, seven_segment_driver_1_a_2, seven_segment_driver_1_b_2, seven_segment_driver_1_c_2,
       seven_segment_driver_1_d_2, seven_segment_driver_1_e, seven_segment_driver_1_f,
       seven_segment_driver_1_g, T_out, tty_control_unit_1_led_changed, tty_control_unit_1_line_check, U_out,
       V_out, W_out, X_out, Y_out, Z_out;
  wire [3:0] adder_1_out, adder_2_out, adder_3_out, adder_4_out, adder_5_out, adder_6_out, adder_7_out,
       bit_extender_1_out, bit_extender_2_out, bit_extender_3_out, bit_extender_4_out, bit_extender_5_out,
       bit_extender_6_out, bit_extender_7_out, bit_extender_8_out;
  wire [4:0] or_5_out;
  wire [6:0] main_1_tty;

  letter_control_unit letter_control_unit_1 (
    .clock(clock_fsm_1_clock), .letter_changed(not_1_out), .letter_first(letter_control_unit_1_letter_first),
    .letter_second(letter_control_unit_1_letter_second), .letter_third(letter_control_unit_1_letter_third));
  not not_1 (not_1_out, comparator_1_eq);
  Button B (.out(B_out));
  Button C (.out(C_out));
  Button D (.out(D_out));
  Button E (.out(E_out));
  Button F (.out(F_out));
  Button G (.out(G_out));
  Button H (.out(H_out));
  Button I (.out(I_out));
  Button J (.out(J_out));
  Button K (.out(K_out));
  Button L (.out(L_out));
  Button M (.out(M_out));
  Button N (.out(N_out));
  Button O (.out(O_out));
  Button P (.out(P_out));
  Button Q (.out(Q_out));
  Button R (.out(R_out));
  Button S (.out(S_out));
  Button T (.out(T_out));
  Button U (.out(U_out));
  Button V (.out(V_out));
  Button W (.out(W_out));
  Button X (.out(X_out));
  Button Y (.out(Y_out));
  Button Z (.out(Z_out));
  tty_control_unit tty_control_unit_1 (
    .letter_equal(main_1_letter_equal_2), .letter_changed(not_1_out),
    .letter_1(letter_control_unit_1_letter_first), .letter_2(letter_control_unit_1_letter_second),
    .letter3(letter_control_unit_1_letter_third), .led_changed(tty_control_unit_1_led_changed),
    .line_check(tty_control_unit_1_line_check));
  clock_fsm clock_fsm_1 (
    .letter_changed(not_1_out), .clock(clock_fsm_1_clock), .tty_display_enable(clock_fsm_1_tty_display_enable));
  Clock clock_1 (.out(clock_fsm_1_clock));
  Comparator #(.width(5)) comparator_1 (.a({5{1'b0}}), .b(or_5_out), .eq(comparator_1_eq));  // open: gt, lt
  control_unit_2 control_unit_2_1 (
    .A(_0_olmali), .B(B_out), .C(C_out), .D(D_out), .E(E_out), .N0(control_unit_2_1_n0),
    .N1(control_unit_2_1_n1), .N2(control_unit_2_1_n2), .N3(control_unit_2_1_n3), .N4(control_unit_2_1_n4));
  control_unit_3 control_unit_3_1 (
    .F(F_out), .G(G_out), .H(H_out), .I(I_out), .J(J_out), .N0(control_unit_3_1_n0),
    .N1(control_unit_3_1_n1), .N2(control_unit_3_1_n2), .N3(control_unit_3_1_n3), .N4(control_unit_3_1_n4));
  control_unit_4 control_unit_4_1 (
    .K(K_out), .L(L_out), .M(M_out), .N(N_out), .O(O_out), .N0(control_unit_4_1_n0),
    .N1(control_unit_4_1_n1), .N2(control_unit_4_1_n2), .N3(control_unit_4_1_n3), .N4(control_unit_4_1_n4));
  control_unit_5 control_unit_5_1 (
    .P(P_out), .Q(Q_out), .R(R_out), .S(S_out), .T(T_out), .N0(control_unit_5_1_n0),
    .N1(control_unit_5_1_n1), .N2(control_unit_5_1_n2), .N3(control_unit_5_1_n3), .N4(control_unit_5_1_n4));
  control_unit_6 control_unit_6_1 (
    .U(U_out), .V(V_out), .W(W_out), .X(X_out), .Y(Y_out), .Z(Z_out), .N0(control_unit_6_1_n0),
    .N1(control_unit_6_1_n1), .N2(control_unit_6_1_n2), .N3(control_unit_6_1_n3), .N4(control_unit_6_1_n4));
  main main_1 (
    ._1(kelime_burdan_verilicek), ._2(in_2), ._3(in_3), ._4(in_4), ._5(in_5), ._6(in_6), ._7(in_7),
    ._8(in_8), .clock(clock_fsm_1_clock), .letter_first(letter_control_unit_1_letter_first),
    .letter_second(letter_control_unit_1_letter_second), .line_check(tty_control_unit_1_line_check),
    .letter_third(letter_control_unit_1_letter_third), .letter_choose(or_5_out),
    .led_check(tty_control_unit_1_led_changed), .a(main_1_a), .b(main_1_b), .c(main_1_c), .d(main_1_d),
    .e(main_1_e), .tty(main_1_tty), .f(main_1_f), .g(main_1_g), .led_1(main_1_led_1), .H(main_1_h),
    .led_2(main_1_led_2), .led_3(main_1_led_3), .letter_equal(main_1_letter_equal),
    .letter_equal_2(main_1_letter_equal_2), .led_4(main_1_led_4), .led_5(main_1_led_5),
    .fail_times(error_times));
  not not_2 (not_2_out, main_1_f);
  not not_3 (not_3_out, main_1_g);
  not not_4 (not_4_out, main_1_h);
  not not_5 (not_5_out, main_1_a);
  not not_6 (not_6_out, main_1_b);
  not not_7 (not_7_out, main_1_c);
  not not_8 (not_8_out, main_1_d);
  not not_9 (not_9_out, main_1_e);
  or or_1 (or_5_out[4], control_unit_2_1_n0, control_unit_4_1_n0, control_unit_6_1_n0, control_unit_5_1_n0, control_unit_3_1_n0);
  or or_2 (or_5_out[3], control_unit_2_1_n1, control_unit_5_1_n1, control_unit_6_1_n1, control_unit_4_1_n1, control_unit_3_1_n1);
  assign bit_extender_1_out = {{3{1'b0}}, not_7_out};  // Bit_Extender bit_extender_1
  assign bit_extender_2_out = {{3{1'b0}}, not_9_out};  // Bit_Extender bit_extender_2
  assign bit_extender_3_out = {{3{1'b0}}, not_3_out};  // Bit_Extender bit_extender_3
  LED led_1 (.in(main_1_led_1));
  LED led_2 (.in(main_1_led_4));
  or or_3 (or_5_out[2], control_unit_2_1_n2, control_unit_4_1_n2, control_unit_6_1_n2, control_unit_5_1_n2, control_unit_3_1_n2);
  assign bit_extender_4_out = {{3{1'b0}}, not_5_out};  // Bit_Extender bit_extender_4
  assign bit_extender_5_out = {{3{1'b0}}, not_6_out};  // Bit_Extender bit_extender_5
  assign bit_extender_6_out = {{3{1'b0}}, not_8_out};  // Bit_Extender bit_extender_6
  assign bit_extender_7_out = {{3{1'b0}}, not_2_out};  // Bit_Extender bit_extender_7
  assign bit_extender_8_out = {{3{1'b0}}, not_4_out};  // Bit_Extender bit_extender_8
  LED led_3 (.in(main_1_led_2));
  LED led_4 (.in(main_1_led_5));
  or or_4 (or_5_out[1], control_unit_2_1_n3, control_unit_4_1_n3, control_unit_6_1_n3, control_unit_5_1_n3, control_unit_3_1_n3);
  TTY tty_1 (.data(main_1_tty), .clk(clock_fsm_1_clock), .we(clock_fsm_1_tty_display_enable));  // open: clr
  Adder #(.width(4)) adder_1 (.a(bit_extender_4_out), .b(bit_extender_5_out), .out(adder_1_out));  // open: cin, cout
  Adder #(.width(4)) adder_2 (.a(bit_extender_1_out), .b(bit_extender_6_out), .out(adder_2_out));  // open: cin, cout
  Adder #(.width(4)) adder_3 (.a(bit_extender_2_out), .b(bit_extender_7_out), .out(adder_3_out));  // open: cin, cout
  Adder #(.width(4)) adder_4 (.a(bit_extender_3_out), .b(bit_extender_8_out), .out(adder_4_out));  // open: cin, cout
  LED led_5 (.in(main_1_led_3));
  or or_5 (or_5_out[0], control_unit_2_1_n4, control_unit_5_1_n4, control_unit_6_1_n4, control_unit_4_1_n4, control_unit_3_1_n4);
  Adder #(.width(4)) adder_5 (.a(adder_1_out), .b(adder_2_out), .out(adder_5_out));  // open: cin, cout
  Adder #(.width(4)) adder_6 (.a(adder_3_out), .b(adder_4_out), .out(adder_6_out));  // open: cin, cout
  Adder #(.width(4)) adder_7 (.a(adder_5_out), .b(adder_6_out), .out(adder_7_out));  // open: cin, cout
  seven_segment_driver seven_segment_driver_1 (
    .D(adder_7_out[3]), .C(adder_7_out[2]), .B(adder_7_out[1]), .A(adder_7_out[0]),
    .a_2(seven_segment_driver_1_a_2), .b_2(seven_segment_driver_1_b_2), .c_2(seven_segment_driver_1_c_2),
    .d_2(seven_segment_driver_1_d_2), .e(seven_segment_driver_1_e), .f(seven_segment_driver_1_f),
    .g(seven_segment_driver_1_g));
  _7_Segment_Display u_7_segment_display_1 (
    .g(seven_segment_driver_1_g), .f(seven_segment_driver_1_f), .a(seven_segment_driver_1_a_2),
    .b(seven_segment_driver_1_b_2), .e(seven_segment_driver_1_e), .d(seven_segment_driver_1_d_2),
    .c(seven_segment_driver_1_c_2));  // open: dp
endmodule

// D B C A
module seven_segment_driver (
  input  D,
  input  C,
  input  B,
  input  A,
  output a_2,
  output b_2,
  output c_2,
  output d_2,
  output e,
  output f,
  output g
);

  wire nand_1_out, nand_2_out, nand_3_out, nand_4_out, nand_5_out, nand_6_out, nand_7_out, nand_8_out,
       nand_9_out, nand_10_out, nand_11_out, nand_12_out, nand_13_out, nand_14_out, nand_15_out, nand_16_out,
       nand_17_out, nand_18_out, nand_19_out, nand_20_out, nand_21_out, nand_22_out, nand_23_out,
       nand_24_out, nand_25_out, nand_26_out, nand_27_out, nand_28_out, nand_29_out, nand_30_out,
       nand_31_out, nand_32_out, nand_33_out, nand_34_out, nand_35_out, nand_36_out, nand_37_out,
       nand_38_out, nand_39_out, nand_40_out, nand_41_out, nand_42_out, nand_43_out, nand_44_out,
       nand_45_out, nand_46_out, nand_47_out, nand_48_out, nand_49_out, nand_50_out, nand_51_out,
       nand_52_out, nand_53_out, nand_54_out, nand_55_out, nand_56_out, nand_57_out, nand_58_out,
       nand_59_out, nand_60_out, nand_61_out, nand_62_out, nand_63_out, nand_64_out, nand_65_out,
       nand_66_out, nand_67_out, nand_68_out, nand_69_out, nand_70_out, nand_71_out, nand_72_out,
       nand_73_out, nand_74_out, nand_75_out, nand_76_out, nand_77_out, nand_78_out, nand_79_out,
       nand_80_out, nand_81_out, nand_82_out, nand_83_out, nand_84_out, nand_85_out, nand_86_out,
       nand_87_out, nand_88_out, nand_89_out, nand_90_out, nand_91_out, nand_92_out, nand_93_out,
       nand_94_out, nand_95_out, nand_96_out, nand_97_out, nand_98_out, nand_99_out, nand_100_out,
       nand_101_out, nand_102_out, nand_103_out, nand_104_out, nand_106_out, nand_107_out, nand_108_out,
       nand_109_out, nand_110_out, nand_111_out, nand_112_out, nand_113_out, nand_114_out, nand_115_out,
       nand_116_out, nand_117_out, nand_118_out, nand_119_out, nand_120_out, nand_121_out, nand_122_out,
       nand_123_out, nand_124_out, nand_125_out, nand_126_out, nand_127_out, nand_128_out, nand_129_out,
       nand_130_out, nand_131_out, nand_132_out, nand_133_out, nand_134_out, nand_136_out, nand_137_out,
       nand_138_out, nand_139_out, nand_141_out, nand_142_out, nand_143_out, nand_144_out, nand_145_out,
       nand_146_out, nand_147_out, nand_148_out;

  nand nand_1 (nand_1_out, C, C);
  nand nand_2 (nand_2_out, D, D);
  nand nand_3 (nand_3_out, B, B);
  nand nand_4 (nand_4_out, D, D);
  nand nand_5 (nand_5_out, B, B);
  nand nand_6 (nand_6_out, D, D);
  nand nand_7 (nand_7_out, D, D);
  nand nand_8 (nand_8_out, C, C);
  nand nand_9 (nand_9_out, C, C);
  nand nand_10 (nand_10_out, C, C);
  nand nand_11 (nand_11_out, A, A);
  nand nand_12 (nand_12_out, A, A);
  nand nand_13 (nand_13_out, D, D);
  nand nand_14 (nand_14_out, C, C);
  nand nand_15 (nand_15_out, A, A);
  nand nand_16 (nand_16_out, D, D);
  nand nand_17 (nand_17_out, D, nand_1_out);
  nand nand_18 (nand_18_out, nand_2_out, nand_3_out);
  nand nand_19 (nand_19_out, nand_4_out, nand_5_out);
  nand nand_20 (nand_20_out, nand_6_out, A);
  nand nand_21 (nand_21_out, nand_7_out, nand_8_out);
  nand nand_22 (nand_22_out, nand_9_out, B);
  nand nand_23 (nand_23_out, nand_10_out, nand_11_out);
  nand nand_24 (nand_24_out, B, nand_12_out);
  nand nand_25 (nand_25_out, D, B);
  nand nand_26 (nand_26_out, D, C);
  nand nand_27 (nand_27_out, nand_13_out, C);
  nand nand_28 (nand_28_out, nand_14_out, B);
  nand nand_29 (nand_29_out, B, nand_15_out);
  nand nand_30 (nand_30_out, nand_16_out, C);
  nand nand_31 (nand_31_out, C, C);
  nand nand_32 (nand_32_out, A, A);
  nand nand_33 (nand_33_out, D, D);
  nand nand_34 (nand_34_out, D, D);
  nand nand_35 (nand_35_out, nand_17_out, nand_17_out);
  nand nand_36 (nand_36_out, B, B);
  nand nand_37 (nand_37_out, D, D);
  nand nand_38 (nand_38_out, C, C);
  nand nand_39 (nand_39_out, nand_18_out, nand_18_out);
  nand nand_40 (nand_40_out, A, A);
  nand nand_41 (nand_41_out, D, D);
  nand nand_42 (nand_42_out, B, B);
  nand nand_43 (nand_43_out, nand_19_out, nand_20_out);
  nand nand_44 (nand_44_out, B, B);
  nand nand_45 (nand_45_out, D, D);
  nand nand_46 (nand_46_out, C, C);
  nand nand_47 (nand_47_out, nand_21_out, nand_21_out);
  nand nand_48 (nand_48_out, A, A);
  nand nand_49 (nand_49_out, nand_22_out, nand_22_out);
  nand nand_50 (nand_50_out, B, B);
  nand nand_51 (nand_51_out, B, B);
  nand nand_52 (nand_52_out, nand_23_out, nand_24_out);
  nand nand_53 (nand_53_out, nand_25_out, nand_26_out);
  nand nand_54 (nand_54_out, B, B);
  nand nand_55 (nand_55_out, A, A);
  nand nand_56 (nand_56_out, nand_27_out, nand_27_out);
  nand nand_57 (nand_57_out, B, B);
  nand nand_58 (nand_58_out, nand_28_out, nand_29_out);
  nand nand_59 (nand_59_out, nand_30_out, nand_30_out);
  nand nand_60 (nand_60_out, B, B);
  nand nand_61 (nand_61_out, C, C);
  nand nand_62 (nand_62_out, nand_31_out, nand_32_out);
  nand nand_63 (nand_63_out, nand_33_out, B);
  nand nand_64 (nand_64_out, nand_34_out, C);
  nand nand_65 (nand_65_out, C, B);
  nand nand_66 (nand_66_out, nand_35_out, nand_36_out);
  nand nand_67 (nand_67_out, nand_37_out, nand_38_out);
  nand nand_68 (nand_68_out, nand_39_out, nand_40_out);
  nand nand_69 (nand_69_out, nand_41_out, B);
  nand nand_70 (nand_70_out, D, nand_42_out);
  nand nand_71 (nand_71_out, nand_43_out, nand_43_out);
  nand nand_72 (nand_72_out, nand_44_out, A);
  nand nand_73 (nand_73_out, nand_45_out, C);
  nand nand_74 (nand_74_out, D, nand_46_out);
  nand nand_75 (nand_75_out, nand_47_out, nand_48_out);
  nand nand_76 (nand_76_out, nand_49_out, A);
  nand nand_77 (nand_77_out, C, nand_50_out);
  nand nand_78 (nand_78_out, C, B);
  nand nand_79 (nand_79_out, D, nand_51_out);
  nand nand_80 (nand_80_out, nand_52_out, nand_52_out);
  nand nand_81 (nand_81_out, nand_53_out, nand_53_out);
  nand nand_82 (nand_82_out, nand_54_out, nand_55_out);
  nand nand_83 (nand_83_out, nand_56_out, nand_57_out);
  nand nand_84 (nand_84_out, nand_58_out, nand_58_out);
  nand nand_85 (nand_85_out, nand_59_out, nand_60_out);
  nand nand_86 (nand_86_out, D, nand_61_out);
  nand nand_87 (nand_87_out, D, A);
  nand nand_88 (nand_88_out, nand_62_out, nand_63_out);
  nand nand_89 (nand_89_out, nand_64_out, nand_64_out);
  nand nand_90 (nand_90_out, nand_65_out, nand_66_out);
  nand nand_91 (nand_91_out, A, A);
  nand nand_92 (nand_92_out, nand_67_out, nand_68_out);
  nand nand_93 (nand_93_out, C, C);
  nand nand_94 (nand_94_out, A, A);
  nand nand_95 (nand_95_out, nand_69_out, nand_69_out);
  nand nand_96 (nand_96_out, nand_70_out, nand_70_out);
  nand nand_97 (nand_97_out, nand_71_out, nand_72_out);
  nand nand_98 (nand_98_out, nand_73_out, nand_74_out);
  nand nand_99 (nand_99_out, nand_75_out, nand_76_out);
  nand nand_100 (nand_100_out, nand_77_out, nand_77_out);
  nand nand_101 (nand_101_out, nand_78_out, nand_78_out);
  nand nand_102 (nand_102_out, A, A);
  nand nand_103 (nand_103_out, nand_79_out, nand_79_out);
  nand nand_104 (nand_104_out, A, A);
  nand nand_105 (e, nand_80_out, nand_81_out);
  nand nand_106 (nand_106_out, nand_82_out, nand_83_out);
  nand nand_107 (nand_107_out, A, A);
  nand nand_108 (nand_108_out, C, C);
  nand nand_109 (nand_109_out, nand_84_out, nand_85_out);
  nand nand_110 (nand_110_out, nand_86_out, nand_87_out);
  nand nand_111 (nand_111_out, nand_88_out, nand_88_out);
  nand nand_112 (nand_112_out, nand_89_out, A);
  nand nand_113 (nand_113_out, nand_90_out, nand_90_out);
  nand nand_114 (nand_114_out, D, nand_91_out);
  nand nand_115 (nand_115_out, nand_92_out, nand_92_out);
  nand nand_116 (nand_116_out, nand_93_out, nand_94_out);
  nand nand_117 (nand_117_out, nand_95_out, A);
  nand nand_118 (nand_118_out, nand_96_out, A);
  nand nand_119 (nand_119_out, nand_97_out, nand_97_out);
  nand nand_120 (nand_120_out, nand_98_out, nand_98_out);
  nand nand_121 (nand_121_out, nand_99_out, nand_99_out);
  nand nand_122 (nand_122_out, nand_100_out, A);
  nand nand_123 (nand_123_out, nand_101_out, nand_102_out);
  nand nand_124 (nand_124_out, nand_103_out, nand_104_out);
  nand nand_125 (nand_125_out, nand_106_out, nand_106_out);
  nand nand_126 (nand_126_out, C, nand_107_out);
  nand nand_127 (nand_127_out, D, nand_108_out);
  nand nand_128 (nand_128_out, D, B);
  nand nand_129 (nand_129_out, nand_109_out, nand_109_out);
  nand nand_130 (nand_130_out, nand_110_out, nand_110_out);
  nand nand_131 (nand_131_out, nand_111_out, nand_112_out);
  nand nand_132 (nand_132_out, nand_113_out, nand_114_out);
  nand nand_133 (nand_133_out, nand_115_out, nand_116_out);
  nand nand_134 (nand_134_out, nand_117_out, nand_118_out);
  nand nand_135 (c_2, nand_119_out, nand_120_out);
  nand nand_136 (nand_136_out, nand_121_out, nand_122_out);
  nand nand_137 (nand_137_out, nand_123_out, nand_124_out);
  nand nand_138 (nand_138_out, nand_125_out, nand_126_out);
  nand nand_139 (nand_139_out, nand_127_out, nand_128_out);
  nand nand_140 (g, nand_129_out, nand_130_out);
  nand nand_141 (nand_141_out, nand_131_out, nand_131_out);
  nand nand_142 (nand_142_out, nand_132_out, nand_132_out);
  nand nand_143 (nand_143_out, nand_133_out, nand_133_out);
  nand nand_144 (nand_144_out, nand_134_out, nand_134_out);
  nand nand_145 (nand_145_out, nand_136_out, nand_136_out);
  nand nand_146 (nand_146_out, nand_137_out, nand_137_out);
  nand nand_147 (nand_147_out, nand_138_out, nand_138_out);
  nand nand_148 (nand_148_out, nand_139_out, nand_139_out);
  nand nand_149 (a_2, nand_141_out, nand_142_out);
  nand nand_150 (b_2, nand_143_out, nand_144_out);
  nand nand_151 (d_2, nand_145_out, nand_146_out);
  nand nand_152 (f, nand_147_out, nand_148_out);
endmodule

module control_unit_2 (
  input  A,
  input  B,
  input  C,
  input  D,
  input  E,
  output N0,
  output N1,
  output N2,
  output N3,
  output N4
);

  wire and_1_out, and_2_out, and_3_out, and_4_out, not_1_out, not_2_out, not_3_out, not_4_out, not_5_out,
       not_6_out, not_7_out, not_8_out, not_9_out, not_10_out, not_11_out, not_12_out;

  not not_1 (not_1_out, A);
  not not_2 (not_2_out, B);
  not not_3 (not_3_out, E);
  not not_4 (not_4_out, A);
  not not_5 (not_5_out, B);
  not not_6 (not_6_out, E);
  not not_7 (not_7_out, A);
  not not_8 (not_8_out, C);
  not not_9 (not_9_out, E);
  not not_10 (not_10_out, A);
  not not_11 (not_11_out, C);
  not not_12 (not_12_out, E);
  and and_1 (and_1_out, not_1_out, not_2_out, D, not_3_out);
  and and_2 (and_2_out, not_4_out, not_5_out, C, not_6_out);
  and and_3 (and_3_out, not_7_out, not_8_out, D, not_9_out);
  and and_4 (and_4_out, not_10_out, B, not_11_out, not_12_out);
  or or_1 (N3, and_1_out, and_2_out);
  or or_2 (N4, and_3_out, and_4_out);

  assign N0 = 1'b0;
  assign N1 = 1'b0;
  assign N2 = E;
endmodule

module control_unit_3 (
  input  F,
  input  G,
  input  H,
  input  I,
  input  J,
  output N0,
  output N1,
  output N2,
  output N3,
  output N4
);

  wire and_1_out, and_2_out, and_3_out, and_4_out, and_5_out, and_6_out, and_7_out, and_8_out, nand_1_out,
       nand_2_out, nand_3_out, nand_4_out, nand_5_out, nand_6_out, nand_7_out, nand_8_out, nand_9_out,
       nand_10_out, not_1_out, not_2_out, not_3_out, not_4_out, not_5_out, not_6_out, not_7_out, not_8_out,
       not_9_out, not_10_out, not_11_out, not_12_out, not_13_out, not_14_out, not_15_out, not_16_out,
       not_17_out, not_18_out;

  nand nand_1 (nand_1_out, F, F);
  nand nand_2 (nand_2_out, G, G);
  nand nand_3 (nand_3_out, H, H);
  nand nand_4 (nand_4_out, I, I);
  nand nand_5 (nand_5_out, F, F);
  nand nand_6 (nand_6_out, G, G);
  nand nand_7 (nand_7_out, H, H);
  nand nand_8 (nand_8_out, J, J);
  not not_1 (not_1_out, I);
  not not_2 (not_2_out, J);
  not not_3 (not_3_out, I);
  not not_4 (not_4_out, J);
  not not_5 (not_5_out, I);
  not not_6 (not_6_out, J);
  not not_7 (not_7_out, F);
  not not_8 (not_8_out, I);
  not not_9 (not_9_out, J);
  not not_10 (not_10_out, F);
  not not_11 (not_11_out, I);
  not not_12 (not_12_out, J);
  not not_13 (not_13_out, G);
  not not_14 (not_14_out, I);
  not not_15 (not_15_out, G);
  not not_16 (not_16_out, I);
  not not_17 (not_17_out, G);
  not not_18 (not_18_out, I);
  nand nand_9 (nand_9_out, nand_1_out, nand_2_out, nand_3_out, nand_4_out, J);
  nand nand_10 (nand_10_out, nand_5_out, nand_6_out, nand_7_out, I, nand_8_out);
  and and_1 (and_1_out, H, not_1_out, not_2_out);
  and and_2 (and_2_out, G, not_3_out, not_4_out);
  and and_3 (and_3_out, F, not_5_out, not_6_out);
  and and_4 (and_4_out, not_7_out, H, not_8_out, not_9_out);
  and and_5 (and_5_out, not_10_out, G, not_11_out, not_12_out);
  and and_6 (and_6_out, not_13_out, not_14_out, J);
  and and_7 (and_7_out, not_15_out, H, not_16_out);
  and and_8 (and_8_out, F, not_17_out, not_18_out);
  nand nand_11 (N1, nand_9_out, nand_10_out);
  or or_1 (N2, and_1_out, and_2_out, and_3_out);
  or or_2 (N3, and_4_out, and_5_out);
  or or_3 (N4, and_6_out, and_7_out, and_8_out);

  assign N0 = 1'b0;
endmodule

module control_unit_4 (
  input  K,
  input  L,
  input  M,
  input  N,
  input  O,
  output N0,
  output N1,
  output N2,
  output N3,
  output N4
);

  wire and_1_out, and_2_out, and_3_out, and_4_out, and_5_out, and_6_out, and_7_out, and_8_out, not_1_out,
       not_2_out, not_3_out, not_4_out, not_5_out, not_6_out, not_7_out, not_8_out, not_9_out, not_10_out,
       not_11_out, not_12_out, not_13_out, not_14_out, not_15_out, not_16_out, not_17_out, not_18_out;

  or or_1 (N1, O, N, M, L, K);
  not not_1 (not_1_out, K);
  not not_2 (not_2_out, L);
  not not_3 (not_3_out, K);
  not not_4 (not_4_out, L);
  not not_5 (not_5_out, K);
  not not_6 (not_6_out, L);
  not not_7 (not_7_out, M);
  not not_8 (not_8_out, N);
  not not_9 (not_9_out, M);
  not not_10 (not_10_out, N);
  not not_11 (not_11_out, M);
  not not_12 (not_12_out, N);
  not not_13 (not_13_out, K);
  not not_14 (not_14_out, M);
  not not_15 (not_15_out, O);
  not not_16 (not_16_out, K);
  not not_17 (not_17_out, M);
  not not_18 (not_18_out, O);
  and and_1 (and_1_out, not_1_out, not_2_out, O);
  and and_2 (and_2_out, not_3_out, not_4_out, N);
  and and_3 (and_3_out, not_5_out, not_6_out, M);
  and and_4 (and_4_out, not_7_out, not_8_out, O);
  and and_5 (and_5_out, L, not_9_out, not_10_out);
  and and_6 (and_6_out, K, not_11_out, not_12_out);
  and and_7 (and_7_out, not_13_out, not_14_out, N, not_15_out);
  and and_8 (and_8_out, not_16_out, L, not_17_out, not_18_out);
  or or_2 (N2, and_1_out, and_2_out, and_3_out);
  or or_3 (N3, and_4_out, and_5_out, and_6_out);
  or or_4 (N4, and_7_out, and_8_out);

  assign N0 = 1'b0;
endmodule

module control_unit_5 (
  input  P,
  input  Q,
  input  R,
  input  S,
  input  T,
  output N0,
  output N1,
  output N2,
  output N3,
  output N4
);

  wire and_1_out, and_2_out, and_3_out, and_4_out, and_5_out, and_6_out, and_7_out, and_8_out, and_9_out,
       not_1_out, not_2_out, not_3_out, not_4_out, not_5_out;

  or or_1 (N0, T, S, R, Q);
  and and_1 (and_1_out, S, T);
  and and_2 (and_2_out, R, T);
  and and_3 (and_3_out, Q, T);
  not not_1 (not_1_out, Q);
  not not_2 (not_2_out, Q);
  not not_3 (not_3_out, R);
  not not_4 (not_4_out, Q);
  not not_5 (not_5_out, T);
  or or_2 (N2, and_1_out, and_2_out, and_3_out, P);
  and and_4 (and_4_out, not_1_out, T);
  and and_5 (and_5_out, Q, R);
  and and_6 (and_6_out, not_2_out, not_3_out, T);
  and and_7 (and_7_out, not_4_out, R, not_5_out);
  and and_8 (and_8_out, R, S);
  and and_9 (and_9_out, Q, S);
  or or_3 (N3, and_4_out, S, and_5_out, P);
  or or_4 (N4, and_6_out, and_7_out, and_8_out, and_9_out, P);

  assign N1 = P;
endmodule

module control_unit_6 (
  input  U,
  input  V,
  input  W,
  input  X,
  input  Y,
  input  Z,
  output N0,
  output N1,
  output N2,
  output N3,
  output N4
);

  or or_1 (N0, Z, Y, X, W, V, U);
  or or_2 (N1, Z, Y);
  or or_3 (N2, X, W, V, U);
  or or_4 (N3, X, W);
  or or_5 (N4, Z, X, V);
endmodule

// lettter
module letter_control_unit (
  input  clock,
  input  letter_changed,
  output letter_first,
  output letter_second,
  output letter_third
);

  wire and_4_out, and_5_out, and_6_out, and_7_out, and_8_out, and_9_out, and_10_out, and_11_out, and_12_out,
       not_1_out, not_2_out, not_3_out, not_4_out, not_5_out, not_6_out, not_7_out, not_8_out, not_9_out;
  wire [2:0] or_1_out, register_1_q;

  Register #(.width(3)) register_1 (.D(or_1_out), .en(1'b1), .Q(register_1_q), .clk(clock));  // open: clr
  and and_1 (letter_first, register_1_q[0], letter_changed);
  and and_2 (letter_second, register_1_q[1], letter_changed);
  and and_3 (letter_third, register_1_q[2], letter_changed);
  not not_1 (not_1_out, register_1_q[0]);
  not not_2 (not_2_out, register_1_q[1]);
  not not_3 (not_3_out, register_1_q[2]);
  not not_4 (not_4_out, letter_changed);
  not not_5 (not_5_out, register_1_q[1]);
  not not_6 (not_6_out, register_1_q[2]);
  not not_7 (not_7_out, letter_changed);
  not not_8 (not_8_out, register_1_q[2]);
  not not_9 (not_9_out, letter_changed);
  and and_4 (and_4_out, not_1_out, register_1_q[1], register_1_q[2], letter_changed);
  and and_5 (and_5_out, register_1_q[0], not_2_out);
  and and_6 (and_6_out, register_1_q[0], not_3_out);
  and and_7 (and_7_out, register_1_q[0], not_4_out);
  and and_8 (and_8_out, not_5_out, register_1_q[2], letter_changed);
  and and_9 (and_9_out, register_1_q[1], not_6_out);
  and and_10 (and_10_out, register_1_q[1], not_7_out);
  and and_11 (and_11_out, not_8_out, letter_changed);
  and and_12 (and_12_out, register_1_q[2], not_9_out);
  or or_1 (or_1_out[0], and_4_out, and_5_out, and_6_out, and_7_out);
  or or_2 (or_1_out[1], and_8_out, and_9_out, and_10_out);
  or or_3 (or_1_out[2], and_11_out, and_12_out);
endmodule

// tty_control
module tty_control_unit (
  input  letter_equal,
  input  letter_changed,
  input  letter_1,
  input  letter_2,
  input  letter3,
  output led_changed,
  output line_check
);

  not not_1 (led_changed, letter_equal);
  and and_1 (line_check, letter_1, letter_2, letter3);
endmodule

// clock
module clock_fsm (
  input  letter_changed,
  output clock,
  output tty_display_enable
);


  assign tty_display_enable = letter_changed;
endmodule
