// Logisim project proje.circ as structural Verilog
module main (
  input  B1,
  input  B2,
  input  RESET
);

  wire a_2_a, b_2_b, c_2_c, clock_1_out, d_2_d, e_2_e, f_2_f, g_1_g;
  wire [2:0] n0_1_n0, register_1_q;

  LED A (.in(a_2_a));
  A a_2 (.S2(register_1_q[2]), .S1(register_1_q[1]), .S0(register_1_q[0]), .B1(B1), .B2(B2), .a(a_2_a));
  Clock clock_1 (.out(clock_1_out));
  LED B (.in(b_2_b));
  B b_2 (.S2(register_1_q[2]), .S1(register_1_q[1]), .S0(register_1_q[0]), .B1(B1), .B2(B2), .b(b_2_b));
  Register #(.width(3)) register_1 (.D(n0_1_n0), .en(1'b1), .Q(register_1_q), .clk(clock_1_out), .clr(RESET));
  LED C (.in(c_2_c));
  C c_2 (.S2(register_1_q[2]), .S1(register_1_q[1]), .S0(register_1_q[0]), .B1(B1), .B2(B2), .c(c_2_c));
  LED D (.in(d_2_d));
  D d_2 (.S2(register_1_q[2]), .S1(register_1_q[1]), .S0(register_1_q[0]), .B1(B1), .B2(B2), .d(d_2_d));
  LED E (.in(e_2_e));
  N2 n2_1 (.S2(register_1_q[2]), .S1(register_1_q[1]), .S0(register_1_q[0]), .B1(B1), .B2(B2), .N2(n0_1_n0[2]));
  E e_2 (.S2(register_1_q[2]), .S1(register_1_q[1]), .S0(register_1_q[0]), .B1(B1), .B2(B2), .e(e_2_e));
  N1 n1_1 (.S2(register_1_q[2]), .S1(register_1_q[1]), .S0(register_1_q[0]), .B1(B1), .B2(B2), .N1(n0_1_n0[1]));
  LED F (.in(f_2_f));
  F f_2 (.S2(register_1_q[2]), .S1(register_1_q[1]), .S0(register_1_q[0]), .B1(B1), .B2(B2), .f(f_2_f));
  N0 n0_1 (.S2(register_1_q[2]), .S1(register_1_q[1]), .S0(register_1_q[0]), .B1(B1), .B2(B2), .n0(n0_1_n0[0]));
  G g_1 (.S2(register_1_q[2]), .S1(register_1_q[1]), .S0(register_1_q[0]), .B1(B1), .B2(B2), .g(g_1_g));
  LED G_2 (.in(g_1_g));
endmodule

module N2 (
  input  S2,
  input  S1,
  input  S0,
  input  B1,
  input  B2,
  output N2
);

  wire and_1_out, and_2_out, and_3_out, and_4_out, and_5_out, and_6_out, not_1_out, not_2_out, not_3_out,
       not_4_out, not_5_out, not_6_out, not_7_out, not_8_out, not_9_out, not_10_out, not_11_out, not_12_out;

  not not_1 (not_1_out, S2);
  not not_2 (not_2_out, S1);
  not not_3 (not_3_out, S0);
  not not_4 (not_4_out, B2);
  not not_5 (not_5_out, S2);
  not not_6 (not_6_out, B1);
  not not_7 (not_7_out, S1);
  not not_8 (not_8_out, B1);
  not not_9 (not_9_out, S0);
  not not_10 (not_10_out, S1);
  not not_11 (not_11_out, S0);
  not not_12 (not_12_out, B2);
  and and_1 (and_1_out, not_1_out, not_2_out, not_3_out, B1, not_4_out);
  and and_2 (and_2_out, not_5_out, S1, S0, not_6_out, B2);
  and and_3 (and_3_out, S2, not_7_out, not_8_out);
  and and_4 (and_4_out, S2, not_9_out, B1, B2);
  and and_5 (and_5_out, S2, not_10_out, S0);
  and and_6 (and_6_out, S2, S1, not_11_out, not_12_out);
  or or_1 (N2, and_1_out, and_2_out, and_3_out, and_4_out, and_5_out, and_6_out);
endmodule

module N1 (
  input  S2,
  input  S1,
  input  S0,
  input  B1,
  input  B2,
  output N1
);

  wire and_1_out, and_2_out, and_3_out, and_4_out, and_5_out, and_6_out, not_1_out, not_2_out, not_3_out,
       not_4_out, not_5_out, not_6_out, not_7_out, not_8_out, not_9_out, not_10_out, not_11_out, not_12_out;

  not not_1 (not_1_out, S1);
  not not_2 (not_2_out, B1);
  not not_3 (not_3_out, S2);
  not not_4 (not_4_out, S0);
  not not_5 (not_5_out, B1);
  not not_6 (not_6_out, S0);
  not not_7 (not_7_out, B1);
  not not_8 (not_8_out, B2);
  not not_9 (not_9_out, S0);
  not not_10 (not_10_out, S2);
  not not_11 (not_11_out, B2);
  not not_12 (not_12_out, S2);
  and and_1 (and_1_out, not_1_out, S0, not_2_out, B2);
  and and_2 (and_2_out, not_3_out, S1, not_4_out, not_5_out);
  and and_3 (and_3_out, S1, not_6_out, not_7_out, not_8_out);
  and and_4 (and_4_out, S1, not_9_out, B1, B2);
  and and_5 (and_5_out, not_10_out, S1, S0, not_11_out);
  and and_6 (and_6_out, not_12_out, S1, S0, B1);
  or or_1 (N1, and_1_out, and_2_out, and_3_out, and_4_out, and_5_out, and_6_out);
endmodule

module N0 (
  input  S2,
  input  S1,
  input  S0,
  input  B1,
  input  B2,
  output n0
);

  wire and_1_out, and_2_out, and_3_out, and_4_out, and_5_out, and_6_out, and_7_out, not_1_out, not_2_out,
       not_3_out, not_4_out, not_5_out, not_6_out, not_7_out, not_8_out, not_9_out, not_10_out, not_11_out,
       not_12_out, not_13_out, not_14_out, not_15_out, not_16_out;

  not not_1 (not_1_out, S2);
  not not_2 (not_2_out, S0);
  not not_3 (not_3_out, B1);
  not not_4 (not_4_out, S1);
  not not_5 (not_5_out, S0);
  not not_6 (not_6_out, B1);
  not not_7 (not_7_out, S2);
  not not_8 (not_8_out, B1);
  not not_9 (not_9_out, B2);
  not not_10 (not_10_out, S1);
  not not_11 (not_11_out, B1);
  not not_12 (not_12_out, B2);
  not not_13 (not_13_out, S2);
  not not_14 (not_14_out, S1);
  not not_15 (not_15_out, S0);
  not not_16 (not_16_out, B2);
  and and_1 (and_1_out, not_1_out, not_2_out, not_3_out, B2);
  and and_2 (and_2_out, not_4_out, not_5_out, not_6_out, B2);
  and and_3 (and_3_out, not_7_out, S0, not_8_out, not_9_out);
  and and_4 (and_4_out, not_10_out, S0, not_11_out, not_12_out);
  and and_5 (and_5_out, not_13_out, S0, B1, B2);
  and and_6 (and_6_out, not_14_out, S0, B1, B2);
  and and_7 (and_7_out, S1, not_15_out, B1, not_16_out);
  or or_1 (n0, and_1_out, and_2_out, and_3_out, and_4_out, and_5_out, and_6_out, and_7_out);
endmodule

module A (
  input  S2,
  input  S1,
  input  S0,
  input  B1,
  input  B2,
  output a
);

  wire and_1_out, and_2_out, and_3_out, not_1_out, not_2_out, not_3_out, not_4_out, not_5_out, not_6_out;

  not not_1 (not_1_out, S1);
  not not_2 (not_2_out, B1);
  not not_3 (not_3_out, S0);
  not not_4 (not_4_out, B1);
  not not_5 (not_5_out, B2);
  not not_6 (not_6_out, S0);
  and and_1 (and_1_out, S2, not_1_out, S0, not_2_out, B2);
  and and_2 (and_2_out, S2, S1, not_3_out, not_4_out, not_5_out);
  and and_3 (and_3_out, S2, S1, not_6_out, B1, B2);
  or or_1 (a, and_1_out, and_2_out, and_3_out);
endmodule

module B (
  input  S2,
  input  S1,
  input  S0,
  input  B1,
  input  B2,
  output b
);

  wire and_1_out, and_2_out, and_3_out, and_4_out, not_1_out, not_2_out, not_3_out, not_4_out, not_5_out,
       not_6_out, not_7_out, not_8_out, not_9_out;

  not not_1 (not_1_out, S1);
  not not_2 (not_2_out, S0);
  not not_3 (not_3_out, B1);
  not not_4 (not_4_out, S1);
  not not_5 (not_5_out, B1);
  not not_6 (not_6_out, B2);
  not not_7 (not_7_out, S1);
  not not_8 (not_8_out, S0);
  not not_9 (not_9_out, B2);
  and and_1 (and_1_out, S2, not_1_out, not_2_out, not_3_out, B2);
  and and_2 (and_2_out, S2, not_4_out, S0, not_5_out, not_6_out);
  and and_3 (and_3_out, S2, not_7_out, S0, B1, B2);
  and and_4 (and_4_out, S2, S1, not_8_out, B1, not_9_out);
  or or_1 (b, and_1_out, and_2_out, and_3_out, and_4_out);
endmodule

module C (
  input  S2,
  input  S1,
  input  S0,
  input  B1,
  input  B2,
  output c
);

  wire and_1_out, and_2_out, and_3_out, and_4_out, not_1_out, not_2_out, not_3_out, not_4_out, not_5_out,
       not_6_out, not_7_out, not_8_out, not_9_out, not_10_out, not_11_out, not_12_out;

  not not_1 (not_1_out, S2);
  not not_2 (not_2_out, S1);
  not not_3 (not_3_out, S0);
  not not_4 (not_4_out, B2);
  not not_5 (not_5_out, S1);
  not not_6 (not_6_out, S0);
  not not_7 (not_7_out, B1);
  not not_8 (not_8_out, B2);
  not not_9 (not_9_out, S1);
  not not_10 (not_10_out, S0);
  not not_11 (not_11_out, S1);
  not not_12 (not_12_out, B2);
  and and_1 (and_1_out, not_1_out, not_2_out, not_3_out, B1, not_4_out);
  and and_2 (and_2_out, S2, not_5_out, not_6_out, not_7_out, not_8_out);
  and and_3 (and_3_out, S2, not_9_out, not_10_out, B1, B2);
  and and_4 (and_4_out, S2, not_11_out, S0, B1, not_12_out);
  or or_1 (c, and_1_out, and_2_out, and_3_out, and_4_out);
endmodule

module D (
  input  S2,
  input  S1,
  input  S0,
  input  B1,
  input  B2,
  output d
);

  wire and_1_out, and_2_out, and_3_out, and_4_out, and_5_out, and_6_out, not_1_out, not_2_out, not_3_out,
       not_4_out, not_5_out, not_6_out, not_7_out, not_8_out, not_9_out, not_10_out, not_11_out, not_12_out,
       not_13_out, not_14_out, not_15_out, not_16_out, not_17_out, not_18_out;

  not not_1 (not_1_out, S2);
  not not_2 (not_2_out, S1);
  not not_3 (not_3_out, S0);
  not not_4 (not_4_out, B1);
  not not_5 (not_5_out, B2);
  not not_6 (not_6_out, S2);
  not not_7 (not_7_out, S1);
  not not_8 (not_8_out, S0);
  not not_9 (not_9_out, S2);
  not not_10 (not_10_out, S1);
  not not_11 (not_11_out, B2);
  not not_12 (not_12_out, S2);
  not not_13 (not_13_out, B1);
  not not_14 (not_14_out, S1);
  not not_15 (not_15_out, S0);
  not not_16 (not_16_out, B2);
  not not_17 (not_17_out, S0);
  not not_18 (not_18_out, B1);
  and and_1 (and_1_out, not_1_out, not_2_out, not_3_out, not_4_out, not_5_out);
  and and_2 (and_2_out, not_6_out, not_7_out, not_8_out, B1, B2);
  and and_3 (and_3_out, not_9_out, not_10_out, S0, B1, not_11_out);
  and and_4 (and_4_out, not_12_out, S1, S0, not_13_out, B2);
  and and_5 (and_5_out, S2, not_14_out, not_15_out, B1, not_16_out);
  and and_6 (and_6_out, S2, S1, not_17_out, not_18_out, B2);
  or or_1 (d, and_1_out, and_2_out, and_3_out, and_4_out, and_5_out, and_6_out);
endmodule

module E (
  input  S2,
  input  S1,
  input  S0,
  input  B1,
  input  B2,
  output e
);

  wire and_1_out, and_2_out, and_3_out, and_4_out, not_1_out, not_2_out, not_3_out, not_4_out, not_5_out,
       not_6_out, not_7_out, not_8_out, not_9_out, not_10_out, not_11_out, not_12_out, not_13_out;

  not not_1 (not_1_out, S2);
  not not_2 (not_2_out, S1);
  not not_3 (not_3_out, S0);
  not not_4 (not_4_out, B1);
  not not_5 (not_5_out, S2);
  not not_6 (not_6_out, S1);
  not not_7 (not_7_out, B1);
  not not_8 (not_8_out, B2);
  not not_9 (not_9_out, S2);
  not not_10 (not_10_out, S1);
  not not_11 (not_11_out, S2);
  not not_12 (not_12_out, S0);
  not not_13 (not_13_out, B2);
  and and_1 (and_1_out, not_1_out, not_2_out, not_3_out, not_4_out, B2);
  and and_2 (and_2_out, not_5_out, not_6_out, S0, not_7_out, not_8_out);
  and and_3 (and_3_out, not_9_out, not_10_out, S0, B1, B2);
  and and_4 (and_4_out, not_11_out, S1, not_12_out, B1, not_13_out);
  or or_1 (e, and_1_out, and_2_out, and_3_out, and_4_out);
endmodule

module F (
  input  S2,
  input  S1,
  input  S0,
  input  B1,
  input  B2,
  output f
);

  wire and_1_out, and_2_out, and_3_out, and_4_out, not_1_out, not_2_out, not_3_out, not_4_out, not_5_out,
       not_6_out, not_7_out, not_8_out, not_9_out, not_10_out, not_11_out;

  not not_1 (not_1_out, S2);
  not not_2 (not_2_out, S1);
  not not_3 (not_3_out, B1);
  not not_4 (not_4_out, S2);
  not not_5 (not_5_out, S0);
  not not_6 (not_6_out, B1);
  not not_7 (not_7_out, B2);
  not not_8 (not_8_out, S2);
  not not_9 (not_9_out, S0);
  not not_10 (not_10_out, S2);
  not not_11 (not_11_out, B2);
  and and_1 (and_1_out, not_1_out, not_2_out, S0, not_3_out, B2);
  and and_2 (and_2_out, not_4_out, S1, not_5_out, not_6_out, not_7_out);
  and and_3 (and_3_out, not_8_out, S1, not_9_out, B1, B2);
  and and_4 (and_4_out, not_10_out, S1, S0, B1, not_11_out);
  or or_1 (f, and_1_out, and_2_out, and_3_out, and_4_out);
endmodule

module G (
  input  S2,
  input  S1,
  input  S0,
  input  B1,
  input  B2,
  output g
);

  wire and_1_out, and_2_out, and_3_out, not_1_out, not_2_out, not_3_out, not_4_out, not_5_out, not_6_out,
       not_7_out;

  not not_1 (not_1_out, S2);
  not not_2 (not_2_out, S0);
  not not_3 (not_3_out, B1);
  not not_4 (not_4_out, S2);
  not not_5 (not_5_out, B1);
  not not_6 (not_6_out, B2);
  not not_7 (not_7_out, S2);
  and and_1 (and_1_out, not_1_out, S1, not_2_out, not_3_out, B2);
  and and_2 (and_2_out, not_4_out, S1, S0, not_5_out, not_6_out);
  and and_3 (and_3_out, not_7_out, S1, S0, B1, B2);
  or or_1 (g, and_1_out, and_2_out, and_3_out);
endmodule
