// Logisim project control.circ as structural Verilog: 1 circuit, main circuit control
module control (
  input  c_output,
  input  add_or_shift,
  input  s_overflow_o,
  input  clock,
  output first_time,
  output shifter_overflow,
  output add_or_shift_2,
  output shifter_for_add,
  output comperator_input
);

  and and_1 (shifter_overflow, s_overflow_o, 1'b1);
  and and_2 (add_or_shift_2, 1'b1, add_or_shift);
  and and_3 (shifter_for_add, 1'b1, add_or_shift);
  and and_4 (comperator_input, c_output, 1'b1);
  Register #(.width(1)) register_1 (.D(1'b1), .en(1'b1), .Q(first_time), .clk(clock));  // open: clr
endmodule
