// Logisim project datapath.circ as structural Verilog: 2 circuits, main circuit main
module main (
  input  Firts_time,
  input  [31:0] INPUT,
  input  comperator_input,
  input  shifter_overflow,
  input  add_or_shift,
  input  clock,
  input  [31:0] MULTIPLICAND,
  input  shfiter_for_add,
  output shifter_overflow_out,
  output add_or_shift_output,
  output comperator_O,
  output [31:0] OUTPUT_second,
  output [31:0] OUTPUT_first
);

  wire and_1_out, not_1_out;
  wire [5:0] counter_1_q;
  wire [31:0] adder_1_out, adder_2_out, demultiplexer_1_out0, demultiplexer_2_out0, demultiplexer_2_out1,
       demultiplexer_3_out0, demultiplexer_3_out1, demultiplexer_4_out0, demultiplexer_4_out1,
       multiplexer_1_out, multiplexer_2_out, multiplexer_3_out, multiplexer_4_out, register_1_q,
       register_2_q, shifter_1_out;

  and and_1 (and_1_out, clock, not_1_out);
  not not_1 (not_1_out, comperator_O);
  Register #(.width(32)) register_1 (.D(OUTPUT_first), .en(1'b1), .Q(register_1_q), .clk(and_1_out));  // open: clr
  Counter #(.width(6), .max('h3f)) counter_1 (.Q(counter_1_q), .clk(and_1_out));  // open: load, D, count, carry, clr
  Multiplexer #(.width(32)) multiplexer_1 (
    .in0(INPUT), .in1(multiplexer_4_out), .out(multiplexer_1_out), .sel(Firts_time), .en(1'b1));
  Demultiplexer #(.width(32)) demultiplexer_1 (
    .out0(demultiplexer_1_out0), .out1(OUTPUT_second), .in(multiplexer_1_out), .sel(comperator_input),
    .en(1'b1));
  Register #(.width(32)) register_2 (
    .D(demultiplexer_1_out0), .en(1'b1), .Q(register_2_q), .clk(and_1_out));  // open: clr
  comparator comparator_1 (
    .in_1(counter_1_q[0]), .in_2(counter_1_q[1]), .in_3(counter_1_q[2]), .in_4(counter_1_q[3]),
    .in_5(counter_1_q[4]), .in_6(counter_1_q[5]), .out_7(comperator_O));
  BitSelector #(.width(32)) bitselector_1 (.in(register_2_q), .out(add_or_shift_output), .sel({5{1'b0}}));
  Demultiplexer #(.width(32)) demultiplexer_2 (
    .out0(demultiplexer_2_out0), .out1(demultiplexer_2_out1), .in(register_1_q), .sel(add_or_shift), .en(1'b1));
  Demultiplexer #(.width(32)) demultiplexer_3 (
    .out0(demultiplexer_3_out0), .out1(demultiplexer_3_out1), .in(register_2_q), .sel(add_or_shift), .en(1'b1));
  Multiplexer #(.width(32)) multiplexer_2 (
    .in0(demultiplexer_2_out0), .in1(adder_1_out), .out(multiplexer_2_out), .sel(shfiter_for_add), .en(1'b1));
  BitSelector #(.width(32)) bitselector_2 (.in(multiplexer_2_out), .out(shifter_overflow_out), .sel({5{1'b0}}));
  Multiplexer #(.width(32)) multiplexer_3 (
    .in0(demultiplexer_3_out0), .in1(demultiplexer_3_out1), .out(multiplexer_3_out), .sel(shfiter_for_add),
    .en(1'b1));
  Adder #(.width(32)) adder_1 (.a(demultiplexer_2_out1), .b(MULTIPLICAND), .out(adder_1_out));  // open: cin, cout
  Shifter #(.width(32), .shift("lr")) shifter_1 (.in(multiplexer_3_out), .\dist (5'b00001), .out(shifter_1_out));
  Shifter #(.width(32), .shift("lr")) shifter_2 (.in(multiplexer_2_out), .\dist (5'b00001), .out(OUTPUT_first));
  Demultiplexer #(.width(32)) demultiplexer_4 (
    .out0(demultiplexer_4_out0), .out1(demultiplexer_4_out1), .in(shifter_1_out), .sel(shifter_overflow),
    .en(1'b1));
  Multiplexer #(.width(32)) multiplexer_4 (
    .in0(demultiplexer_4_out0), .in1(adder_2_out), .out(multiplexer_4_out), .sel(shifter_overflow), .en(1'b1));
  Adder #(.width(32)) adder_2 (.a(demultiplexer_4_out1), .b(32'h80000000), .out(adder_2_out));  // open: cin, cout
endmodule

module comparator (
  input  in_1,
  input  in_2,
  input  in_3,
  input  in_4,
  input  in_5,
  input  in_6,
  output out_7
);

  wire and_1_out, and_2_out, or_1_out, xnor_1_out, xnor_2_out, xnor_3_out, xnor_4_out, xnor_5_out, xnor_6_out;

  xnor xnor_1 (xnor_1_out, 1'b0, in_2);
  xnor xnor_2 (xnor_2_out, 1'b0, in_3);
  xnor xnor_3 (xnor_3_out, 1'b0, in_4);
  xnor xnor_4 (xnor_4_out, 1'b0, in_5);
  xnor xnor_5 (xnor_5_out, 1'b1, in_6);
  or or_1 (or_1_out, in_5, in_4, in_3, in_2, in_1);
  xnor xnor_6 (xnor_6_out, 1'b0, in_1);
  and and_1 (and_1_out, xnor_5_out, or_1_out);
  and and_2 (and_2_out, xnor_6_out, xnor_1_out, xnor_2_out, xnor_3_out, xnor_4_out, xnor_5_out);
  or or_2 (out_7, and_2_out, and_1_out);
endmodule
